# Fritzing sketch schematic (saved by Fritzing 0.9.3b)
circuit board: 13.513cm x 6.85095cm
circuit board: 13.513cm x 6.85095cm

parts:
  ARDUINO1 = Arduino Uno (Rev3)
  LCD = female pin header, 10 pins [form="♀ (female)"]
  S1 = Toggle Switch [package=THT]
  LED1 = LED - 3mm [color="Red (633nm)" package="3 mm [THT]"]
  R1 = Resistor [tolerance=±5% resistance=210 package=THT]
  R3 = Resistor [tolerance=±5% resistance=10k package=THT]
  R4 = Resistor [tolerance=±5% resistance=10k package=THT]
  R5 = Resistor [tolerance=±5% resistance=10k package=THT]
  R6 = Resistor [tolerance=±5% resistance=10k package=THT]
  LCD1 = female pin header, 10 pins [form="♀ (female)"]  # not connected

nets:
  N1: ARDUINO1.D8, LCD.pin8
  N2: ARDUINO1.D9_PWM, LCD.pin7
  N3: ARDUINO1.D10_PWM/SS, LCD.pin5
  N4: ARDUINO1.D11_PWM/MOSI, LCD.pin4
  N5: ARDUINO1.D13/SCK, LCD.pin3
  N6: ARDUINO1.GND, LCD.pin10, LED1.cathode, R6.Pin_1
  N7: ARDUINO1.5V, LCD.pin1, LCD.pin9, S1.L2, R1.Pin_0
  N8: LED1.anode, R1.Pin_1
  N9: R3.Pin_0, R5.Pin_1
  N10: R3.Pin_1, R6.Pin_0
  N11: R4.Pin_0, R5.Pin_0

notes:
  Miguel Cardoso Leirosa Nº18 12ºEAC 2016/2017 EPG
  Jogador 1
  Jogador 2

// code stored in the sketch: Untitled Sketch.fzz.ino

